# Fritzing sketch RP2040_Recorder (saved by Fritzing 0.9.3b)
breadboards: 1

parts:
  Mod1 = Raspberry Pi Pico
  S1 = Pushbutton [package="[SMD]"]
  MIC = Breakout Board for Electret Microphone
  LED1 = LEDs [package=led10mm]
  C1 = Ceramic Capacitor [capacitance=100nF package="200 mil [THT, multilayer]"]
  SD = Micro SD card reader
  R1 = Resistor [tolerance=±5% resistance=150 package="0805 [SMD]"]
  R2 = Resistor [tolerance=±5% resistance=1k package="2010 [SMD]"]

nets:
  N1: Mod1.pin_3, Mod1.pin_8, Mod1.pin_13, Mod1.pin_18, Mod1.pin_23, Mod1.pin_28, Mod1.pin_33, Mod1.pin_38, S1.Pin_1, S1.Pin_2, MIC.GND, SD.Pin_6, R1.Pin_0
  N2: Mod1.pin_16, S1.Pin_3, S1.Pin_4, R2.Pin_1
  N3: Mod1.pin_17, LED1.A
  N4: Mod1.pin_21, SD.Pin_5
  N5: Mod1.pin_22, SD.Pin_2
  N6: Mod1.pin_24, SD.Pin_4
  N7: Mod1.pin_25, SD.Pin_3
  N8: Mod1.pin_31, C1.1
  N9: Mod1.pin_36, MIC.VCC, R2.Pin_0
  N10: MIC.AUD, C1.0
  N11: LED1.C, R1.Pin_1

custom parts:
  Raspberry Pi Pico: Raspberry Pi Pico. Based around the RP2040 microcontroller the Pico is a low cost microcontroller device bringing Raspberry Pi quality, cost, and easy of use to the microcontroller space. Jan 2021, Split part in to two versions: tht (this one) and SMD. This one will drill holes for a .1 in header in pcb to allow plugging in the module as well as providing pads to solder the module to the top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
  Micro SD card reader: Micro SD card reader.
